# Fritzing sketch dht22-i2c-lcd (saved by Fritzing 0.9.6b)
breadboards: 1

parts:
  M1 = DOIT Esp32 DevKit v1 (30 pins long, 11 pins width) [part_number=ESP32S-PIN30]
  A1 = DHT22 module
  OLED1 = OLED 128x64 I2C Monochrome Display

nets:
  3V3: M1.3V3, A1.+, OLED1.VDD
  GND: M1.GND, A1.-, OLED1.GND
  N1: M1.D4, A1.Out
  N2: M1.D21, OLED1.SDA
  N3: M1.D22, OLED1.SCK

custom parts:
  DOIT Esp32 DevKit v1 (30 pins long, 11 pins width): The DOIT Esp32 DevKit v1 is one of the development board created by DOIT to evaluate the ESP-WROOM-32 module. It is based on the ESP32 microcontroller that boasts Wifi, Bluetooth, Ethernet and Low Power support all in a single chip. (vanepp) made breadboard work, adjusted pin numbering and labels and reduced size of schematic and cleaned up pcb. This chip is 30pins long (2 x15) and 11 pins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
  DHT22 module: DHT22 module. Pins VCC Data GND.
